# Fritzing sketch LCD_Exercises (saved by Fritzing 0.7.11b)
breadboards: 1

parts:
  U1 = LCD - 12pins [chip_label=LCD package="SIP (Single Inline) [THT]"]
  Arduino1 = Arduino
  IC1 = IC, DIP package, 16 pins [chip_label=74HC4050]

nets:
  N1: U1.VBATT, Arduino1.+5V
  3.3V: U1.3.3V, Arduino1.3V3, IC1.pin1
  GND: U1.GND, Arduino1.GND, IC1.pin8
  N2: U1.STAT0, Arduino1.D2
  N3: U1.STAT1, Arduino1.D3
  N4: U1.STAT2, Arduino1.D4
  N5: U1.RESET, IC1.pin2
  N6: U1.DIO, IC1.pin6
  N7: U1.SCK, IC1.pin10
  N8: U1.CS, IC1.pin4
  N9: U1.S2, Arduino1.D6
  N10: U1.S1, Arduino1.D5
  N11: Arduino1.D13, IC1.pin9
  N12: Arduino1.D11, IC1.pin7
  N13: Arduino1.D9, IC1.pin5
  N14: Arduino1.D8, IC1.pin3

custom parts:
  LCD - 12pins: A SIP stand-in part for whatever you want. With 12 pins on a 300 mil single inline package (SIP) footprint.
